# Fritzing sketch map (saved by Fritzing 0.9.3b)
circuit board: 8.46667cm x 5.64444cm
breadboards: 1

parts:
  7_Segment1 = 7 Segment Display
  VCC1 = Battery
  Part1 = Arduino Nano (Rev3.0)

nets:
  N1: 7_Segment1.Segment_G, Part1.D5
  N2: 7_Segment1.Segment_F, Part1.D4
  N3: 7_Segment1.common_anode, VCC1.+, Part1.VIN
  N4: 7_Segment1.Segment_E, Part1.D3
  N5: 7_Segment1.Segment_D, Part1.D2
  N6: 7_Segment1.Segment_DP, Part1.D6
  N7: 7_Segment1.Segment_C, Part1.D7
  N8: 7_Segment1.Segment_B, Part1.D8
  N9: 7_Segment1.Segment_A, Part1.D9
  N10: VCC1.-, Part1.GND
